// Logisim project 27 Bit Arithmatic Logic Unit.circ as structural Verilog: 14 circuits, main circuit main
module main (
);


  // Notes on the sheet:
  //   2207024
endmodule

// AND
module _27_Bit_AND (
  input  [26:0] A,
  input  [26:0] B,
  output [26:0] AB
);

  assign AB = A & B;  // AND_Gate and_1, 27 bits wide

  // Notes on the sheet:
  //   2207024
endmodule

// OR
module _27_Bit_OR (
  input  [26:0] A,
  input  [26:0] B,
  output [26:0] A_B
);

  assign A_B = A | B;  // OR_Gate or_1, 27 bits wide

  // Notes on the sheet:
  //   2207024
endmodule

// Zero
module Zero_Check (
  input  [26:0] A,
  output out_2
);

  wire or_1_out;

  or or_1 (or_1_out, A[0], A[1], A[2], A[3], A[4], A[5], A[6], A[7], A[8], A[9], A[10], A[11], A[12], A[13], A[14], A[15], A[16], A[17], A[18], A[19], A[20], A[21], A[22], A[23], A[24], A[25], A[26]);
  not not_1 (out_2, or_1_out);

  // Notes on the sheet:
  //   2207024
endmodule

module Negative_check (
  input  [26:0] A,
  output out_2
);


  assign out_2 = A[26];

  // Notes on the sheet:
  //   2207024
endmodule

module _3_bit_CLA_adder___subtractor (
  input  Cin,
  input  [2:0] A,
  input  [2:0] B,
  output s0,
  output s1,
  output s2,
  output c3,
  output c2
);

  wire and_4_out, and_5_out, and_6_out, and_7_out, and_8_out, and_9_out, C1, G0, G1, G2, P0, P1, P2;

  xor xor_1 (P0, B[0], A[0]);
  xor xor_2 (P1, B[1], A[1]);
  xor xor_3 (P2, B[2], A[2]);
  and and_1 (G0, B[0], A[0]);
  and and_2 (G1, B[1], A[1]);
  and and_3 (G2, B[2], A[2]);
  and and_4 (and_4_out, Cin, P0);
  and and_5 (and_5_out, G0, P1);
  and and_6 (and_6_out, P1, Cin, P0);
  and and_7 (and_7_out, G1, P2);
  and and_8 (and_8_out, P2, G0, P1);
  or or_1 (C1, and_4_out, G0);
  and and_9 (and_9_out, P0, P1, P2, Cin);
  or or_2 (c2, and_5_out, and_6_out, G1);
  or or_3 (c3, and_7_out, and_8_out, G2, and_9_out);
  _1_Bit_full_Adder u_1_bit_full_adder_1 (.A(A[0]), .B(B[0]), .C_in(Cin), .S(s0));
  _1_Bit_full_Adder u_1_bit_full_adder_2 (.A(A[1]), .B(B[1]), .C_in(C1), .S(s1));
  _1_Bit_full_Adder u_1_bit_full_adder_3 (.A(A[2]), .B(B[2]), .C_in(c2), .S(s2));

  // Notes on the sheet:
  //   2207024
endmodule

module _9_bit_cla_adder___sub (
  input  in_1,
  input  [8:0] A,
  input  [8:0] B,
  output [8:0] out_4,
  output out_5,
  output out_6
);

  wire n3_bit_cla_adder_subtractor_1_c3, n3_bit_cla_adder_subtractor_2_c3;

  _3_bit_CLA_adder___subtractor u_3_bit_cla_adder_subtractor_1 (
    .Cin(in_1), .A(A[2:0]), .B(B[2:0]), .s0(out_4[0]), .s1(out_4[1]), .s2(out_4[2]),
    .c3(n3_bit_cla_adder_subtractor_1_c3));  // open: c2
  _3_bit_CLA_adder___subtractor u_3_bit_cla_adder_subtractor_2 (
    .Cin(n3_bit_cla_adder_subtractor_1_c3), .A(A[5:3]), .B(B[5:3]), .s0(out_4[3]), .s1(out_4[4]),
    .s2(out_4[5]), .c3(n3_bit_cla_adder_subtractor_2_c3));  // open: c2
  _3_bit_CLA_adder___subtractor u_3_bit_cla_adder_subtractor_3 (
    .Cin(n3_bit_cla_adder_subtractor_2_c3), .A(A[8:6]), .B(B[8:6]), .c2(out_6), .s0(out_4[6]), .s1(out_4[7]),
    .s2(out_4[8]), .c3(out_5));

  // Notes on the sheet:
  //   2207024
endmodule

module _27_bit_CLA_adder__subtractor (
  input  in_1,
  input  [26:0] A,
  input  [26:0] B,
  output [26:0] out_4,
  output out_5,
  output out_6
);

  wire n9_bit_cla_adder_sub_1_out_5, n9_bit_cla_adder_sub_2_out_5, n9_bit_cla_adder_sub_3_out_6;
  wire [26:0] bit_extender_1_out, xor_1_out;

  assign xor_1_out = B ^ bit_extender_1_out;  // XOR_Gate xor_1, 27 bits wide
  assign bit_extender_1_out = {{26{in_1}}, in_1};  // Bit_Extender bit_extender_1
  _9_bit_cla_adder___sub u_9_bit_cla_adder_sub_1 (
    .in_1(in_1), .A(A[8:0]), .B(xor_1_out[8:0]), .out_4(out_4[8:0]), .out_5(n9_bit_cla_adder_sub_1_out_5));  // open: out_6
  _9_bit_cla_adder___sub u_9_bit_cla_adder_sub_2 (
    .in_1(n9_bit_cla_adder_sub_1_out_5), .A(A[17:9]), .B(xor_1_out[17:9]), .out_4(out_4[17:9]),
    .out_5(n9_bit_cla_adder_sub_2_out_5));  // open: out_6
  _9_bit_cla_adder___sub u_9_bit_cla_adder_sub_3 (
    .in_1(n9_bit_cla_adder_sub_2_out_5), .A(A[26:18]), .B(xor_1_out[26:18]),
    .out_6(n9_bit_cla_adder_sub_3_out_6), .out_4(out_4[26:18]), .out_5(out_5));
  xor xor_2 (out_6, n9_bit_cla_adder_sub_3_out_6, out_5);

  // Notes on the sheet:
  //   2207024
endmodule

module _27_BIT_ALU (
  input  [1:0] in_1,
  input  [26:0] A,
  input  [26:0] B,
  output [26:0] out_4,
  output out_5,
  output out_6,
  output out_7,
  output out_8
);

  wire [26:0] n27_bit_and_1_ab, n27_bit_cla_adder_subtractor_1_out_4, n27_bit_or_1_a_b;

  _27_bit_CLA_adder__subtractor u_27_bit_cla_adder_subtractor_1 (
    .in_1(in_1[0]), .A(A), .B(B), .out_6(out_8), .out_4(n27_bit_cla_adder_subtractor_1_out_4), .out_5(out_7));
  _27_Bit_AND u_27_bit_and_1 (.A(A), .B(B), .AB(n27_bit_and_1_ab));
  _27_Bit_OR u_27_bit_or_1 (.A(A), .B(B), .A_B(n27_bit_or_1_a_b));
  Multiplexer #(.select(2), .width(27)) multiplexer_1 (
    .in0(n27_bit_and_1_ab), .in1(n27_bit_or_1_a_b), .in2(n27_bit_cla_adder_subtractor_1_out_4),
    .in3(n27_bit_cla_adder_subtractor_1_out_4), .out(out_4), .sel(in_1));  // open: en
  Zero_Check zero_check_1 (.A(out_4), .out_2(out_5));
  Negative_check negative_check_1 (.A(out_4), .out_2(out_6));

  // Notes on the sheet:
  //   A
  //   B
  //   2207024
  //   CONTROL
  //   CONTROL
  //   OUTPUT
  //   ZERO FLAG
  //   NEGATIVE FLAG
  //   CARRY FLAG
  //   Overflow Flag
  //   00
  //   01
  //   10
  //   11
  //   FUNCTION
  //   - AND
  //   - OR
  //   - ADDER
  //   - SUBTRACTOR
endmodule

module controller (
  input  [1:0] Q,
  input  [2:0] T,
  input  C,
  output DA,
  output DB,
  output DC
);

  wire and_1_out, and_2_out, and_3_out, and_4_out, and_5_out, or_4_out, or_5_out, Q0, Q1, Q2, Q3, T0, T1, T2,
       T3, T4, T5, T6, T7;

  Decoder #(.select(2), .enable("false")) decoder_1 (.out0(Q0), .out1(Q1), .out2(Q2), .out3(Q3), .sel(Q));
  Decoder #(.select(3), .enable("false")) decoder_2 (
    .out0(T0), .out1(T1), .out2(T2), .out3(T3), .out4(T4), .out5(T5), .out6(T6), .out7(T7), .sel(T));
  or or_1 (DA, T0, and_5_out, T3, T4, and_1_out, T7);
  or or_2 (DB, T1, and_2_out, T5, T6, T6, T7);
  or or_3 (DC, T5, and_3_out, T3, T4, and_4_out, T7);
  and and_1 (and_1_out, T6, C);
  and and_2 (and_2_out, T2, Q2);
  and and_3 (and_3_out, T2, or_4_out);
  and and_4 (and_4_out, T6, C);
  and and_5 (and_5_out, T2, or_5_out);
  or or_4 (or_4_out, Q0, Q1, Q3);
  or or_5 (or_5_out, Q0, Q2, Q3);

  // Notes on the sheet:
  //   2207024
endmodule

module sequence_detector (
  input  Clk,
  input  Reset,
  input  Q0,
  input  Q_1,
  input  [4:0] Count,
  output Cl__A__Q_1,
  output LOad__M__Q__Cnt,
  output Load_A,
  output C0,
  output C1,
  output Shr,
  output Dec_Cnt
);

  wire cnt, controller_1_da, controller_1_db, controller_1_dc, T0, T2, T4, T6, T7;
  wire [2:0] T;

  nor nor_1 (cnt, Count[0], Count[1], Count[2], Count[3], Count[4]);
  controller controller_1 (
    .Q({Q0, Q_1}), .T(T), .C(cnt), .DA(controller_1_da), .DB(controller_1_db), .DC(controller_1_dc));
  D_Flip_Flop d_ff_1 (.clk(Clk), .D(controller_1_da), .Q(T[0]), .reset(Reset));  // open: Qn, preset, en
  D_Flip_Flop d_ff_2 (.clk(Clk), .D(controller_1_db), .Q(T[1]), .reset(Reset));  // open: Qn, preset, en
  D_Flip_Flop d_ff_3 (.clk(Clk), .D(controller_1_dc), .Q(T[2]), .reset(Reset));  // open: Qn, preset, en
  or or_1 (Load_A, C0, T4);
  or or_2 (C1, T4, C0);
  Decoder #(.select(3), .enable("false")) decoder_1 (
    .out0(T0), .out1(Cl__A__Q_1), .out2(T2), .out3(C0), .out4(T4), .out5(Dec_Cnt), .out6(T6), .out7(T7),
    .sel(T));

  assign LOad__M__Q__Cnt = Cl__A__Q_1;
  assign Shr = Dec_Cnt;

  // Other names for the same wires on the sheet: T1 = Cl__A__Q_1; T3 = C0; T5 = Dec_Cnt

  // Notes on the sheet:
  //   2207024
endmodule

module booths_algorithm (
  input  [26:0] M,
  input  [26:0] Q,
  input  Reset,
  output [26:0] out_4,
  output [26:0] out_5
);

  wire A_out, c0, c1, CL, clk, DEC, load, load_m_q_cnt, or_1_out, Q_1, Q_out, shr;
  wire [4:0] count;
  wire [26:0] m_t, n27_bit_alu_1_out_4;

  Clock u_CLK (.out(clk));
  sequence_detector sequence_detector_1 (
    .Clk(clk), .Reset(Reset), .Q0(out_5[0]), .Q_1(Q_1), .Count(count), .Cl__A__Q_1(CL),
    .LOad__M__Q__Cnt(load_m_q_cnt), .Load_A(load), .C0(c0), .C1(c1), .Shr(shr), .Dec_Cnt(DEC));
  or or_1 (or_1_out, load_m_q_cnt, DEC);
  Counter #(.width(5), .max('h1b)) counter_1 (
    .load(or_1_out), .D(5'b11011), .count(DEC), .Q(count), .clk(clk));  // open: carry, clr
  Shift_Register #(.length(27)) A (
    .shift(shr), .in(out_4[26]), .clk(clk), .out(A_out), .load(load), .clr(CL), .d0(n27_bit_alu_1_out_4[26]),
    .q0(out_4[26]), .d1(n27_bit_alu_1_out_4[25]), .q1(out_4[25]), .d2(n27_bit_alu_1_out_4[24]),
    .q2(out_4[24]), .d3(n27_bit_alu_1_out_4[23]), .q3(out_4[23]), .d4(n27_bit_alu_1_out_4[22]),
    .q4(out_4[22]), .d5(n27_bit_alu_1_out_4[21]), .q5(out_4[21]), .d6(n27_bit_alu_1_out_4[20]),
    .q6(out_4[20]), .d7(n27_bit_alu_1_out_4[19]), .q7(out_4[19]), .d8(n27_bit_alu_1_out_4[18]),
    .q8(out_4[18]), .d9(n27_bit_alu_1_out_4[17]), .q9(out_4[17]), .d10(n27_bit_alu_1_out_4[16]),
    .q10(out_4[16]), .d11(n27_bit_alu_1_out_4[15]), .q11(out_4[15]), .d12(n27_bit_alu_1_out_4[14]),
    .q12(out_4[14]), .d13(n27_bit_alu_1_out_4[13]), .q13(out_4[13]), .d14(n27_bit_alu_1_out_4[12]),
    .q14(out_4[12]), .d15(n27_bit_alu_1_out_4[11]), .q15(out_4[11]), .d16(n27_bit_alu_1_out_4[10]),
    .q16(out_4[10]), .d17(n27_bit_alu_1_out_4[9]), .q17(out_4[9]), .d18(n27_bit_alu_1_out_4[8]),
    .q18(out_4[8]), .d19(n27_bit_alu_1_out_4[7]), .q19(out_4[7]), .d20(n27_bit_alu_1_out_4[6]),
    .q20(out_4[6]), .d21(n27_bit_alu_1_out_4[5]), .q21(out_4[5]), .d22(n27_bit_alu_1_out_4[4]),
    .q22(out_4[4]), .d23(n27_bit_alu_1_out_4[3]), .q23(out_4[3]), .d24(n27_bit_alu_1_out_4[2]),
    .q24(out_4[2]), .d25(n27_bit_alu_1_out_4[1]), .q25(out_4[1]), .d26(n27_bit_alu_1_out_4[0]), .q26(out_4[0]));
  _27_BIT_ALU u_27_bit_alu_1 (
    .in_1({c1, c0}), .A(out_4), .B(m_t), .out_4(n27_bit_alu_1_out_4));  // open: out_5, out_6, out_7, out_8
  Shift_Register #(.length(27)) u_Q (
    .shift(shr), .in(A_out), .clk(clk), .out(Q_out), .load(load_m_q_cnt), .d0(Q[26]), .q0(out_5[26]),
    .d1(Q[25]), .q1(out_5[25]), .d2(Q[24]), .q2(out_5[24]), .d3(Q[23]), .q3(out_5[23]), .d4(Q[22]),
    .q4(out_5[22]), .d5(Q[21]), .q5(out_5[21]), .d6(Q[20]), .q6(out_5[20]), .d7(Q[19]), .q7(out_5[19]),
    .d8(Q[18]), .q8(out_5[18]), .d9(Q[17]), .q9(out_5[17]), .d10(Q[16]), .q10(out_5[16]), .d11(Q[15]),
    .q11(out_5[15]), .d12(Q[14]), .q12(out_5[14]), .d13(Q[13]), .q13(out_5[13]), .d14(Q[12]),
    .q14(out_5[12]), .d15(Q[11]), .q15(out_5[11]), .d16(Q[10]), .q16(out_5[10]), .d17(Q[9]), .q17(out_5[9]),
    .d18(Q[8]), .q18(out_5[8]), .d19(Q[7]), .q19(out_5[7]), .d20(Q[6]), .q20(out_5[6]), .d21(Q[5]),
    .q21(out_5[5]), .d22(Q[4]), .q22(out_5[4]), .d23(Q[3]), .q23(out_5[3]), .d24(Q[2]), .q24(out_5[2]),
    .d25(Q[1]), .q25(out_5[1]), .d26(Q[0]), .q26(out_5[0]));  // open: clr
  Shift_Register #(.length(27)) u_M (
    .shift(1'b0), .clk(clk), .load(load_m_q_cnt), .d0(M[26]), .q0(m_t[26]), .d1(M[25]), .q1(m_t[25]),
    .d2(M[24]), .q2(m_t[24]), .d3(M[23]), .q3(m_t[23]), .d4(M[22]), .q4(m_t[22]), .d5(M[21]), .q5(m_t[21]),
    .d6(M[20]), .q6(m_t[20]), .d7(M[19]), .q7(m_t[19]), .d8(M[18]), .q8(m_t[18]), .d9(M[17]), .q9(m_t[17]),
    .d10(M[16]), .q10(m_t[16]), .d11(M[15]), .q11(m_t[15]), .d12(M[14]), .q12(m_t[14]), .d13(M[13]),
    .q13(m_t[13]), .d14(M[12]), .q14(m_t[12]), .d15(M[11]), .q15(m_t[11]), .d16(M[10]), .q16(m_t[10]),
    .d17(M[9]), .q17(m_t[9]), .d18(M[8]), .q18(m_t[8]), .d19(M[7]), .q19(m_t[7]), .d20(M[6]), .q20(m_t[6]),
    .d21(M[5]), .q21(m_t[5]), .d22(M[4]), .q22(m_t[4]), .d23(M[3]), .q23(m_t[3]), .d24(M[2]), .q24(m_t[2]),
    .d25(M[1]), .q25(m_t[1]), .d26(M[0]), .q26(m_t[0]));  // open: in, out, clr
  Shift_Register #(.length(1)) Q__1 (.shift(shr), .in(Q_out), .clk(clk), .clr(CL), .q0(Q_1));  // open: out, load, d0

  // Other names for the same wires on the sheet: MM[26:0] = M; Q0 = out_5[0]; qq[26:0] = out_5

  // Notes on the sheet:
  //   output
  //   2207024
endmodule

module _123 (
  input  Clk,
  input  Reset,
  input  Q0,
  input  Q_1,
  input  [2:0] Count,
  output Cl__A__Q_1,
  output LOad__M__Q__Cnt,
  output Load_A,
  output C0,
  output C1,
  output Shr,
  output Dec_Cnt
);

  wire and_3_out, multiplexer_1_out, not_1_out, not_2_out, not_3_out, not_4_out, not_5_out, not_6_out,
       not_7_out, or_2_out, Q0_prime_Q_1_out, Q0Q_1_prime_out;
  wire [1:0] rom_1_data_2;
  wire [2:0] and_1_out, and_2_out, bit_extender_1_out, bit_extender_2_out, bit_extender_3_out, CAR_q,
       or_1_out, rom_1_data;

  assign bit_extender_1_out = {{2{Q0_prime_Q_1_out}}, Q0_prime_Q_1_out};  // Bit_Extender bit_extender_1
  and Q0_prime_Q_1 (Q0_prime_Q_1_out, not_2_out, Q_1);
  not not_1 (not_1_out, Q0_prime_Q_1_out);
  assign bit_extender_2_out = {{2{not_1_out}}, not_1_out};  // Bit_Extender bit_extender_2
  assign and_1_out = 3'b100 & bit_extender_3_out & bit_extender_1_out;  // AND_Gate and_1, 3 bits wide
  assign or_1_out = and_1_out | rom_1_data | and_2_out;  // OR_Gate or_1, 3 bits wide
  not not_2 (not_2_out, Q0);
  assign and_2_out = bit_extender_2_out & bit_extender_3_out & 3'b101;  // AND_Gate and_2, 3 bits wide
  assign bit_extender_3_out = {{2{and_3_out}}, and_3_out};  // Bit_Extender bit_extender_3
  and and_3 (and_3_out, not_4_out, CAR_q[1], not_3_out);
  not not_3 (not_3_out, CAR_q[0]);
  not not_4 (not_4_out, CAR_q[2]);
  Counter #(.width(3), .max('h7)) CAR (
    .load(not_5_out), .D(or_1_out), .count(multiplexer_1_out), .Q(CAR_q), .clk(Clk), .clr(Reset));  // open: carry
  not not_5 (not_5_out, multiplexer_1_out);
  Multiplexer #(.select(2), .enable("false")) multiplexer_1 (
    .in0(1'b0), .in1(1'b1), .in2(Q0Q_1_prime_out), .in3(not_7_out), .out(multiplexer_1_out),
    .sel(rom_1_data_2));
  ROM #(.addrWidth(3), .dataWidth(12)) rom_1 (
    .addr(CAR_q), .data({Cl__A__Q_1, LOad__M__Q__Cnt, Load_A, C0, C1, Shr, Dec_Cnt, rom_1_data, rom_1_data_2}));  // open: sel
  and Q0Q_1_prime (Q0Q_1_prime_out, not_6_out, Q0);
  not not_6 (not_6_out, Q_1);
  not not_7 (not_7_out, or_2_out);
  or or_2 (or_2_out, Count[0], Count[1], Count[2]);

  // Notes on the sheet:
  //   To choose only
  //   state 2 (010)
  //   Control Word Format: Clear (A, Q-1), Load (M, Q, Cnt), Load A, C0, C1, Shr, Dec Cnt, Address bits (3 bit), Selection bits (2 bit)
  //   contents of rom_1 (hex, n*v repeats v):
  //   1 c01 2 394 281 61 b 1c
  //   2207024
endmodule

module _1_Bit_full_Adder (
  input  A,
  input  B,
  input  C_in,
  output S
);

  wire xor_1_out;

  xor xor_1 (xor_1_out, A, B);
  xor xor_2 (S, xor_1_out, C_in);
endmodule
