// Logisim project 3 bit Binary Adder.circ as structural Verilog: 2 circuits, main circuit main
module main (
  input  A0,
  input  B1,
  input  A1,
  input  A2,
  input  in_5,
  input  B0,
  input  in_7
);

  wire adder_1_out_5, adder_1_sum, adder_2_out_5, adder_2_sum, adder_3_out_5, adder_3_sum;

  ADDER adder_1 (.in_1(A0), .in_2(B0), .in_3(in_7), .SUM(adder_1_sum), .out_5(adder_1_out_5));
  LED led_1 (.in(adder_1_sum));
  ADDER adder_2 (.in_1(A1), .in_2(B1), .in_3(adder_1_out_5), .SUM(adder_2_sum), .out_5(adder_2_out_5));
  LED led_2 (.in(adder_2_sum));
  LED led_3 (.in(adder_3_sum));
  ADDER adder_3 (.in_1(in_5), .in_2(A2), .in_3(adder_2_out_5), .SUM(adder_3_sum), .out_5(adder_3_out_5));
  LED led_4 (.in(adder_3_out_5));

  // Notes on the sheet:
  //   S
  //   S
  //   B2
  //   S
  //   C
endmodule

module ADDER (
  input  in_1,
  input  in_2,
  input  in_3,
  output SUM,
  output out_5
);

  wire and_1_out, and_2_out, and_3_out;

  ExactlyOne xor_1 (.out(SUM), .in0(in_1), .in1(in_2), .in2(in_3));
  and and_1 (and_1_out, in_1, in_2);
  and and_2 (and_2_out, in_2, in_3);
  and and_3 (and_3_out, in_1, in_3);
  or or_1 (out_5, and_1_out, and_2_out, and_3_out);

  // Notes on the sheet:
  //   A
  //   B
  //   Cin
  //   carry
endmodule
