// Logisim project 4 Bit Multiplier.circ as structural Verilog: 3 circuits, main circuit main
module main (
  input  [3:0] A,
  input  [3:0] B,
  output [7:0] MULTIPLE
);

  wire and_1_out, and_2_out, and_3_out, and_4_out, and_6_out, and_7_out, and_8_out, and_9_out, and_10_out,
       and_11_out, and_12_out, and_13_out, and_14_out, and_15_out, and_16_out, full_adder_1_cout,
       full_adder_1_sum, full_adder_2_cout, full_adder_2_sum, full_adder_3_cout, full_adder_3_sum,
       full_adder_4_cout, full_adder_4_sum, full_adder_5_cout, full_adder_5_sum, full_adder_6_cout,
       full_adder_7_cout, half_adder_1_carry, half_adder_2_carry, half_adder_2_sum, half_adder_3_carry,
       half_adder_4_carry;

  and and_1 (and_1_out, B[2], A[0]);
  and and_2 (and_2_out, B[2], A[1]);
  and and_3 (and_3_out, B[2], A[2]);
  and and_4 (and_4_out, B[2], A[3]);
  and and_5 (MULTIPLE[0], B[0], A[0]);
  and and_6 (and_6_out, B[0], A[1]);
  and and_7 (and_7_out, B[0], A[2]);
  and and_8 (and_8_out, B[0], A[3]);
  and and_9 (and_9_out, B[1], A[0]);
  and and_10 (and_10_out, B[1], A[1]);
  and and_11 (and_11_out, B[1], A[2]);
  and and_12 (and_12_out, B[1], A[3]);
  and and_13 (and_13_out, B[3], A[0]);
  and and_14 (and_14_out, B[3], A[1]);
  and and_15 (and_15_out, B[3], A[2]);
  and and_16 (and_16_out, B[3], A[3]);
  half_adder half_adder_1 (.A(and_9_out), .B(and_6_out), .Sum(MULTIPLE[1]), .Carry(half_adder_1_carry));
  full_adder full_adder_1 (
    .A(and_7_out), .B(half_adder_1_carry), .Cin(and_10_out), .Sum(full_adder_1_sum), .Cout(full_adder_1_cout));
  full_adder full_adder_2 (
    .A(and_8_out), .B(full_adder_1_cout), .Cin(and_11_out), .Sum(full_adder_2_sum), .Cout(full_adder_2_cout));
  half_adder half_adder_2 (.A(and_12_out), .B(full_adder_2_cout), .Sum(half_adder_2_sum), .Carry(half_adder_2_carry));
  half_adder half_adder_3 (.A(and_1_out), .B(full_adder_1_sum), .Sum(MULTIPLE[2]), .Carry(half_adder_3_carry));
  full_adder full_adder_3 (
    .A(and_2_out), .B(full_adder_2_sum), .Cin(half_adder_3_carry), .Sum(full_adder_3_sum),
    .Cout(full_adder_3_cout));
  full_adder full_adder_4 (
    .A(full_adder_3_cout), .B(and_3_out), .Cin(half_adder_2_sum), .Sum(full_adder_4_sum),
    .Cout(full_adder_4_cout));
  full_adder full_adder_5 (
    .A(full_adder_4_cout), .B(half_adder_2_carry), .Cin(and_4_out), .Sum(full_adder_5_sum),
    .Cout(full_adder_5_cout));
  half_adder half_adder_4 (.A(and_13_out), .B(full_adder_3_sum), .Sum(MULTIPLE[3]), .Carry(half_adder_4_carry));
  full_adder full_adder_6 (
    .A(and_14_out), .B(full_adder_4_sum), .Cin(half_adder_4_carry), .Sum(MULTIPLE[4]),
    .Cout(full_adder_6_cout));
  full_adder full_adder_7 (
    .A(full_adder_6_cout), .B(and_15_out), .Cin(full_adder_5_sum), .Sum(MULTIPLE[5]), .Cout(full_adder_7_cout));
  full_adder full_adder_8 (
    .A(full_adder_7_cout), .B(full_adder_5_cout), .Cin(and_16_out), .Sum(MULTIPLE[6]), .Cout(MULTIPLE[7]));

  // Notes on the sheet:
  //   2207024
  //   A3 A2 A1 A0
  //   B3 B2 B1 B0
endmodule

// HA
module half_adder (
  input  A,
  input  B,
  output Sum,
  output Carry
);

  and and_1 (Carry, A, B);
  xor xor_1 (Sum, A, B);

  // Notes on the sheet:
  //   2207024
  //   B
  //   A
  //   Half Adder
endmodule

// FA
module full_adder (
  input  A,
  input  B,
  input  Cin,
  output Sum,
  output Cout
);

  wire and_1_out, and_2_out, xor_1_out;

  xor xor_1 (xor_1_out, A, B);
  and and_1 (and_1_out, xor_1_out, Cin);
  and and_2 (and_2_out, A, B);
  xor xor_2 (Sum, xor_1_out, Cin);
  or or_1 (Cout, and_1_out, and_2_out);

  // Notes on the sheet:
  //   2207024
  //   A
  //   Cin
  //   B
  //   Full Adder
endmodule
