// Logisim project Adder & Subtractor for 4 bit.circ as structural Verilog: 4 circuits, main circuit main
module main (
  input  in_1,
  input  in_2,
  input  in_3,
  input  in_4,
  input  in_5,
  input  in_6,
  input  in_7,
  input  in_8,
  input  in_9,
  input  in_10,
  output out_11,
  output out_12,
  output out_13,
  output out_14,
  output out_15,
  output out_16,
  output out_17,
  output out_18,
  output out_19,
  output out_20
);

  Adder_as_subtractor adder_as_subtractor_1 (
    .Bout(out_15), .in_5(in_1), .in_6(in_2), .in_7(in_3), .in_8(in_4), .in_1(in_5), .in_2(in_6),
    .y3_y2_y1_y0(in_7), .in_4(in_8), .out_10(out_11), .out_11(out_12), .d3_d2_d1_d0(out_13), .out_13(out_14),
    .Borrow(in_9));
  Adder_as_subtractor adder_as_subtractor_2 (
    .Bout(out_20), .in_5(in_1), .in_6(in_2), .in_7(in_3), .in_8(in_4), .in_1(in_5), .in_2(in_6),
    .y3_y2_y1_y0(in_7), .in_4(in_8), .out_10(out_16), .out_11(out_17), .d3_d2_d1_d0(out_18), .out_13(out_19),
    .Borrow(in_10));

  // Notes on the sheet:
  //   x3 x2 x1 x0
  //   y3 y2 y1 y0
  //   when carry in is 0 it acts as a adder
  //   when carry in is 1 it acts as a subtractor
endmodule

module Adder (
  input  A__B__Cin,
  input  in_2,
  input  in_3,
  output Cout,
  output SUM
);

  wire and_1_out, and_2_out, xor_1_out;

  xor xor_1 (xor_1_out, A__B__Cin, in_2);
  ExactlyOne xor_2 (.out(SUM), .in0(A__B__Cin), .in1(in_2), .in2(in_3));
  and and_1 (and_1_out, xor_1_out, in_3);
  and and_2 (and_2_out, A__B__Cin, in_2);
  or or_1 (Cout, and_1_out, and_2_out);
endmodule

module _4_bit_parallel_adder (
  input  in_1,
  input  in_2,
  input  y3_y2_y1_y0,
  input  in_4,
  input  in_5,
  input  in_6,
  input  in_7,
  input  in_8,
  input  cin,
  output out_10,
  output out_11,
  output s3_s2_s1_s0,
  output out_13,
  output cout
);

  wire adder_2_cout, adder_3_cout, adder_4_cout;

  Adder adder_1 (.Cout(cout), .A__B__Cin(in_5), .in_2(in_1), .SUM(out_10), .in_3(adder_2_cout));
  Adder adder_2 (.Cout(adder_2_cout), .A__B__Cin(in_6), .in_2(in_2), .SUM(out_11), .in_3(adder_3_cout));
  Adder adder_3 (.Cout(adder_3_cout), .A__B__Cin(in_7), .in_2(y3_y2_y1_y0), .SUM(s3_s2_s1_s0), .in_3(adder_4_cout));
  Adder adder_4 (.Cout(adder_4_cout), .A__B__Cin(in_8), .in_2(in_4), .SUM(out_13), .in_3(cin));

  // Notes on the sheet:
  //   x3 x2 x1 x0
endmodule

// Adder/ Subtractor
module Adder_as_subtractor (
  input  in_1,
  input  in_2,
  input  y3_y2_y1_y0,
  input  in_4,
  input  in_5,
  input  in_6,
  input  in_7,
  input  in_8,
  input  Borrow,
  output out_10,
  output out_11,
  output d3_d2_d1_d0,
  output out_13,
  output Bout
);

  wire xor_1_out, xor_2_out, xor_3_out, xor_4_out;

  xor xor_1 (xor_1_out, Borrow, in_1);
  _4_bit_parallel_adder u_4_bit_parallel_adder_1 (
    .cout(Bout), .in_5(in_5), .in_6(in_6), .in_7(in_7), .in_8(in_8), .in_1(xor_1_out), .in_2(xor_4_out),
    .y3_y2_y1_y0(xor_3_out), .in_4(xor_2_out), .out_10(out_10), .out_11(out_11), .s3_s2_s1_s0(d3_d2_d1_d0),
    .out_13(out_13), .cin(Borrow));
  xor xor_2 (xor_2_out, in_4, Borrow);
  xor xor_3 (xor_3_out, y3_y2_y1_y0, Borrow);
  xor xor_4 (xor_4_out, Borrow, in_2);

  // Notes on the sheet:
  //   x3 x2 x1 x0
endmodule
