// Logisim project Displaying 2207024 with Counter.circ as structural Verilog: 1 circuit, main circuit main
module main (
  input  in_1,
  output out_2,
  output out_3,
  output out_4
);

  wire and_1_out, and_2_out, and_3_out, and_4_out, and_5_out, and_6_out, and_7_out, clock_1_out, not_1_out,
       not_2_out, not_3_out, not_4_out, or_1_out, or_2_out, or_3_out, or_4_out, t_ff_1_q, t_ff_2_q;

  and and_1 (and_1_out, out_3, t_ff_1_q);
  or or_1 (or_1_out, and_1_out, and_2_out);
  Clock clock_1 (.out(clock_1_out));
  and and_2 (and_2_out, out_2, out_3);
  and and_3 (and_3_out, not_1_out, not_2_out, out_3);
  not not_1 (not_1_out, t_ff_1_q);
  not not_2 (not_2_out, out_2);
  T_Flip_Flop t_ff_1 (.clk(clock_1_out), .T(or_1_out), .Q(t_ff_1_q), .reset(in_1));  // open: Qn, preset, en
  not not_3 (not_3_out, t_ff_1_q);
  T_Flip_Flop t_ff_2 (.clk(clock_1_out), .T(and_3_out), .Q(t_ff_2_q), .reset(in_1));  // open: Qn, preset, en
  or or_2 (or_2_out, and_5_out, and_4_out, out_2);
  and and_4 (and_4_out, t_ff_1_q, out_3);
  and and_5 (and_5_out, not_3_out, not_4_out);
  not not_4 (not_4_out, out_3);
  T_Flip_Flop t_ff_3 (.clk(clock_1_out), .T(or_2_out), .Q(out_2), .reset(in_1));  // open: Qn, preset, en
  or or_3 (or_3_out, not_4_out, t_ff_1_q, t_ff_2_q, out_2);
  T_Flip_Flop t_ff_4 (.clk(clock_1_out), .T(or_3_out), .Q(out_3), .reset(in_1));  // open: Qn, preset, en
  or or_4 (or_4_out, and_7_out, and_6_out);
  and and_6 (and_6_out, not_2_out, not_3_out, not_4_out);
  and and_7 (and_7_out, out_3, out_2);
  T_Flip_Flop t_ff_5 (.clk(clock_1_out), .T(or_4_out), .Q(out_4), .reset(in_1));  // open: Qn, preset, en

  // Notes on the sheet:
  //   E
  //   D
  //   C
  //   B
  //   A
  //   2207024
  //   T1
  //   T2
  //   A
  //   B
  //   T3
  //   C
  //   T4
  //   D
  //   E 
endmodule
