// Logisim project Gray to Binary Code Converter Using Different Gates.circ as structural Verilog: 4 circuits, main circuit main
module main (
  input  A,
  input  B,
  input  in_3,
  output out_4,
  output out_5,
  output out_6,
  output out_7,
  output out_8,
  output out_9,
  output out_10,
  output out_11,
  output out_12,
  output out_13,
  output out_14,
  output out_15
);

  wire and_1_out, and_2_out, and_3_out, and_4_out, NAND_2_out_3, NAND_3_out_3, NAND_4_out_3, NAND_5_out_3,
       NAND_6_out_3, NAND_out_3, nor_1_out_3, nor_2_out_3, nor_3_out_3, nor_4_out_3, nor_5_out_3,
       nor_6_out_3, nor_7_out_3, nor_8_out_3, not_1_out, not_2_out, not_3_out, not_4_out;

  NOR nor_1 (.A(A), .B(B), .out_3(nor_1_out_3));
  NOR nor_2 (.A(out_11), .B(in_3), .out_3(nor_2_out_3));
  not not_1 (not_1_out, A);
  not not_2 (not_2_out, in_3);
  NAND NAND (.A(A), .B(B), .out_3(NAND_out_3));
  NAND NAND_2 (.A(out_5), .B(in_3), .out_3(NAND_2_out_3));
  NOR nor_3 (.A(A), .B(nor_1_out_3), .out_3(nor_3_out_3));
  NOR nor_4 (.A(nor_1_out_3), .B(B), .out_3(nor_4_out_3));
  NOR nor_5 (.A(out_11), .B(nor_2_out_3), .out_3(nor_5_out_3));
  NOR nor_6 (.A(nor_2_out_3), .B(in_3), .out_3(nor_6_out_3));
  not not_3 (not_3_out, B);
  not not_4 (not_4_out, out_14);
  NAND NAND_3 (.A(A), .B(NAND_out_3), .out_3(NAND_3_out_3));
  NAND NAND_4 (.A(NAND_out_3), .B(B), .out_3(NAND_4_out_3));
  NAND NAND_5 (.A(out_5), .B(NAND_2_out_3), .out_3(NAND_5_out_3));
  NAND NAND_6 (.A(NAND_2_out_3), .B(in_3), .out_3(NAND_6_out_3));
  XOR xor_1 (.B(A), .A(B), .out_3(out_8));
  XOR xor_2 (.B(in_3), .A(out_8), .out_3(out_9));
  NOR nor_7 (.A(nor_3_out_3), .B(nor_4_out_3), .out_3(nor_7_out_3));
  NOR nor_8 (.A(nor_5_out_3), .B(nor_6_out_3), .out_3(nor_8_out_3));
  NOR nor_9 (.A(nor_7_out_3), .B(nor_7_out_3), .out_3(out_11));
  NOR nor_10 (.A(nor_8_out_3), .B(nor_8_out_3), .out_3(out_12));
  and and_1 (and_1_out, A, not_3_out);
  and and_2 (and_2_out, B, not_1_out);
  and and_3 (and_3_out, in_3, not_4_out);
  and and_4 (and_4_out, out_14, not_2_out);
  NAND NAND_7 (.A(NAND_3_out_3), .B(NAND_4_out_3), .out_3(out_5));
  NAND NAND_8 (.A(NAND_5_out_3), .B(NAND_6_out_3), .out_3(out_6));
  or or_1 (out_14, and_1_out, and_2_out);
  or or_2 (out_15, and_3_out, and_4_out);

  assign out_4 = A;
  assign out_7 = A;
  assign out_10 = A;
  assign out_13 = A;

  // Notes on the sheet:
  //   2207024
  //   GRAY CODE
  //   C
  //   B
  //   A
  //   C
  //   NOT
  //   NOT
  //   NOR
  //   NOR
  //   A'
  //   C'
  //   NOT
  //   XOR
  //   NOR
  //   NOR
  //   NOR
  //   NOR
  //   B'
  //   NOT
  //   (A XOR B)'
  //   XOR
  //   NOR
  //   NOR
  //   AB'
  //   A'B
  //   (AB'+A'B)' C
  //   (AB'+A'B) C'
  //   AND
  //   NOR
  //   NOR
  //   AND
  //   AND
  //   AND
  //   AB'+A'B
  //   A XOR B
  //   (AB'+A'B) C'+ (AB'+A'B)'C
  //   A XOR B XOR C
  //   OR
  //   BINARY CODE (USING NOR GATE)
  //   OR
  //   BINARY CODE (USING NAND GATE)
  //   BINARY CODE (USING XOR GATE)
  //   BINARY CODE USING BASIC GATES(AND ,OR,NOT)
endmodule

module NAND (
  input  A,
  input  B,
  output out_3
);

  wire and_1_out;

  and and_1 (and_1_out, A, B);
  not not_1 (out_3, and_1_out);

  // Notes on the sheet:
  //   AND
  //   NOT
  //   NAND
endmodule

module NOR (
  input  A,
  input  B,
  output out_3
);

  wire or_1_out;

  or or_1 (or_1_out, A, B);
  not not_1 (out_3, or_1_out);

  // Notes on the sheet:
  //   OR
  //   NOT
endmodule

module XOR (
  input  B,
  input  A,
  output out_3
);

  wire and_1_out, and_2_out, not_1_out, not_2_out;

  not not_1 (not_1_out, A);
  not not_2 (not_2_out, B);
  and and_1 (and_1_out, A, not_2_out);
  and and_2 (and_2_out, B, not_1_out);
  or or_1 (out_3, and_1_out, and_2_out);

  // Notes on the sheet:
  //   A'
  //   B'
  //   A XOR B
endmodule
