// Logisim project Printing Roll with 7 segment display.circ as structural Verilog: 1 circuit, main circuit main
module main (
  input  in_1,
  input  in_2
);

  wire and_1_out, and_2_out, and_3_out, and_4_out, and_5_out, and_6_out, and_7_out, and_8_out, and_9_out,
       and_10_out, and_11_out, main_1_out_2, main_1_out_3, main_1_out_4, not_1_out, not_2_out, not_3_out,
       not_4_out, or_1_out, or_2_out, or_3_out, or_4_out, or_5_out, or_6_out, or_7_out;

  not not_1 (not_1_out, in_2);
  not not_2 (not_2_out, main_1_out_2);
  not not_3 (not_3_out, main_1_out_3);
  not not_4 (not_4_out, main_1_out_4);
  and and_1 (and_1_out, main_1_out_3, main_1_out_4);
  and and_2 (and_2_out, not_3_out, not_4_out);
  or or_1 (or_1_out, main_1_out_2, not_3_out, main_1_out_4);
  and and_3 (and_3_out, not_2_out, main_1_out_3);
  and and_4 (and_4_out, main_1_out_3, not_4_out);
  and and_5 (and_5_out, not_2_out, not_4_out);
  and and_6 (and_6_out, main_1_out_2, not_3_out, main_1_out_4);
  and and_7 (and_7_out, main_1_out_2, not_3_out);
  Displaying_2207024_with_Counter_main main_1 (
    .out_2(main_1_out_2), .out_3(main_1_out_3), .out_4(main_1_out_4), .in_1(in_1));
  and and_8 (and_8_out, main_1_out_2, not_4_out);
  and and_9 (and_9_out, main_1_out_2, main_1_out_4);
  and and_10 (and_10_out, not_2_out, not_4_out);
  and and_11 (and_11_out, not_2_out, main_1_out_3);
  or or_2 (or_2_out, not_2_out, and_1_out, and_2_out);
  or or_3 (or_3_out, and_4_out, and_5_out);
  or or_4 (or_4_out, in_2, main_1_out_3, and_9_out, and_10_out);
  or or_5 (or_5_out, and_4_out, and_7_out, and_11_out, in_2);
  or or_6 (or_6_out, in_2, and_2_out, and_7_out, and_8_out);
  _7_Segment_Display u_7_segment_display_1 (
    .g(or_5_out), .f(or_6_out), .a(or_4_out), .b(or_2_out), .e(or_3_out), .d(or_7_out), .c(or_1_out));  // open: dp
  or or_7 (or_7_out, in_2, and_3_out, and_4_out, and_5_out, and_6_out);

  // Notes on the sheet:
  //   a
  //   b
  //   c
  //   d
endmodule
